// Logisim project mips_in_logisim.circ as structural Verilog: 5 circuits, main circuit main
module main (
  output [31:0] out_1,
  output [23:0] out_2,
  output [31:0] dados_indo_pro_acc,
  output [31:0] dados_da_ula
);

  wire caminho_de_controle_en_mon, caminho_de_controle_en_ram, caminho_de_controle_en_tec,
       caminho_de_controle_rd_ram, caminho_de_controle_sel_op2, caminho_de_controle_sel_ula,
       caminho_de_controle_wr_acc, caminho_de_controle_wr_ram, clock_1_out;
  wire [1:0] caminho_de_controle_sel_op_0;
  wire [5:0] caminho_de_dados_caminho_de_controle;
  wire [6:0] keyboard_1_data;
  wire [23:0] caminho_de_controle_a_rom;
  wire [31:0] ram_1_data, rom_1_data;

  Clock clock_1 (.out(clock_1_out));
  caminho_de_dados caminho_de_dados (
    .DOUT_TEC(keyboard_1_data), .DOUT_ROM(rom_1_data), .DOUT_BUS(ram_1_data),
    .SEL_OP2(caminho_de_controle_sel_op2), .SEL_OP1(caminho_de_controle_sel_op_0),
    .WR_ACC(caminho_de_controle_wr_acc), .SEL_ULA(caminho_de_controle_sel_ula),
    .caminho_de_controle(caminho_de_dados_caminho_de_controle), .ADD_IMED(out_2), .CLOCK(clock_1_out),
    .DIN_RAM(out_1), .dados_indo_pro_acc(dados_da_ula), .valor_ula(dados_indo_pro_acc));
  RAM #(.addrWidth(24), .dataWidth(32), .bus("separate")) ram_1 (
    .addr(out_2), .din(out_1), .data(ram_1_data), .str(caminho_de_controle_wr_ram),
    .sel(caminho_de_controle_en_ram), .clk(clock_1_out), .ld(caminho_de_controle_rd_ram));  // open: clr
  caminho_de_controle caminho_de_controle (
    .in_3(caminho_de_dados_caminho_de_controle[5]), .in_4(caminho_de_dados_caminho_de_controle[4]),
    .in_5(caminho_de_dados_caminho_de_controle[3]), .A(caminho_de_dados_caminho_de_controle[2]),
    .B(caminho_de_dados_caminho_de_controle[1]), .C(caminho_de_dados_caminho_de_controle[0]),
    .EN_MON(caminho_de_controle_en_mon), .EN_TEC(caminho_de_controle_en_tec),
    .SEL_ULA(caminho_de_controle_sel_ula), .SEL_OP2(caminho_de_controle_sel_op2),
    .SEL_OP_0(caminho_de_controle_sel_op_0[0]), .SEL_OP_1(caminho_de_controle_sel_op_0[1]),
    .WR_ACC(caminho_de_controle_wr_acc), .RD_RAM(caminho_de_controle_rd_ram),
    .WR_RAM(caminho_de_controle_wr_ram), .EN_RAM(caminho_de_controle_en_ram), .CLOCK(clock_1_out),
    .ADD_IMED(out_2), .A_ROM(caminho_de_controle_a_rom));
  ROM #(.addrWidth(24), .dataWidth(32)) rom_1 (.addr(caminho_de_controle_a_rom), .data(rom_1_data));  // open: sel
  TTY tty_1 (.data(out_1[6:0]), .clk(clock_1_out), .we(caminho_de_controle_en_mon));  // open: clr
  Keyboard keyboard_1 (.clk(clock_1_out), .re(caminho_de_controle_en_tec), .data(keyboard_1_data));  // open: clr, avail

  // Notes on the sheet:
  //   contents of rom_1 (hex, n*v repeats v):
  //   24000000 28000000 14000001 20000001
endmodule

module caminho_de_dados (
  input  [6:0] DOUT_TEC,
  input  [31:0] DOUT_ROM,
  input  [31:0] DOUT_BUS,
  input  CLOCK,
  input  SEL_OP2,
  input  [1:0] SEL_OP1,
  input  WR_ACC,
  input  SEL_ULA,
  output [5:0] caminho_de_controle,
  output [23:0] ADD_IMED,
  output [31:0] DIN_RAM,
  output [31:0] dados_indo_pro_acc,
  output [31:0] valor_ula
);

  wire [25:24] IR_q;
  wire [31:0] bit_extender_1_out, bit_extender_2_out, multiplexer_1_out;

  assign bit_extender_1_out = {{25{1'b0}}, DOUT_TEC};  // Bit_Extender bit_extender_1
  Multiplexer #(.width(32), .enable("false")) multiplexer_1 (
    .in0(bit_extender_2_out), .in1(DOUT_BUS), .out(multiplexer_1_out), .sel(SEL_OP2));
  ula ULA (.entrada_a(DIN_RAM), .entrada_b(multiplexer_1_out), .seletor(SEL_ULA), .saida(valor_ula));
  Register #(.width(32)) IR (.D(DOUT_ROM), .Q({caminho_de_controle, IR_q, ADD_IMED}), .clk(CLOCK));  // open: en, clr
  Multiplexer #(.select(2), .width(32), .enable("false")) multiplexer_2 (
    .in0(valor_ula), .in1(bit_extender_2_out), .in2(DOUT_BUS), .in3(bit_extender_1_out),
    .out(dados_indo_pro_acc), .sel(SEL_OP1));
  Register #(.width(32)) ACC (.D(dados_indo_pro_acc), .en(WR_ACC), .Q(DIN_RAM), .clk(CLOCK));  // open: clr
  assign bit_extender_2_out = {{8{1'b0}}, ADD_IMED};  // Bit_Extender bit_extender_2
endmodule

module caminho_de_controle (
  input  A,
  input  B,
  input  in_3,
  input  in_4,
  input  in_5,
  input  C,
  input  CLOCK,
  input  [23:0] ADD_IMED,
  output EN_RAM,
  output WR_RAM,
  output RD_RAM,
  output WR_ACC,
  output SEL_OP_1,
  output SEL_OP_0,
  output SEL_OP2,
  output SEL_ULA,
  output EN_TEC,
  output EN_MON,
  output [23:0] A_ROM
);

  wire logica_de_controle_1_en_pc, logica_de_controle_1_sel_j;
  wire [23:0] adder_1_out, PC_q;

  logica_de_controle logica_de_controle_1 (
    .in_1(in_3), .in_2(in_4), .A(in_5), .B(A), .C(B), .D(C), .EN_RAM(EN_RAM), .WR_RAM(WR_RAM),
    .RD_RAM(RD_RAM), .EN_PC(logica_de_controle_1_en_pc), .WR_ACC(WR_ACC), .SEL_OP_1(SEL_OP_1),
    .SEL_OP_0(SEL_OP_0), .SEL_OP2(SEL_OP2), .SEL_ULA(SEL_ULA), .SEL_J(logica_de_controle_1_sel_j),
    .SEL_TEC(EN_TEC), .SEL_MON(EN_MON));
  Register #(.width(24)) PC (.D(adder_1_out), .en(logica_de_controle_1_en_pc), .Q(PC_q), .clk(CLOCK));  // open: clr
  Multiplexer #(.width(24), .enable("false")) multiplexer_1 (
    .in0(PC_q), .in1(ADD_IMED), .out(A_ROM), .sel(logica_de_controle_1_sel_j));
  Adder #(.width(24)) adder_1 (.a(A_ROM), .b(24'h1), .out(adder_1_out));  // open: cin, cout
endmodule

module ula (
  input  [31:0] entrada_a,
  input  [31:0] entrada_b,
  input  seletor,
  output [31:0] saida
);

  wire [31:0] adder_1_out, subtractor_1_out;

  Adder #(.width(32)) adder_1 (.a(entrada_a), .b(entrada_b), .out(adder_1_out));  // open: cin, cout
  Subtractor #(.width(32)) subtractor_1 (.a(entrada_a), .b(entrada_b), .out(subtractor_1_out));  // open: bin, bout
  Multiplexer #(.width(32), .enable("false")) multiplexer_1 (
    .in0(adder_1_out), .in1(subtractor_1_out), .out(saida), .sel(seletor));
endmodule

// Logica de controle
module logica_de_controle (
  input  in_1,
  input  in_2,
  input  D,
  input  C,
  input  B,
  input  A,
  output EN_RAM,
  output WR_RAM,
  output RD_RAM,
  output EN_PC,
  output WR_ACC,
  output SEL_OP_1,
  output SEL_OP_0,
  output SEL_OP2,
  output SEL_ULA,
  output SEL_J,
  output SEL_TEC,
  output SEL_MON
);

  wire A_B_out, A_nC_out, and_1_out, and_2_out, and_3_out, and_4_out, B_nC_out, nA_B__C_out, nA_B_nC_out,
       nA_nB_C_out, not_1_out, not_2_out, not_3_out, not_4_out, not_5_out, not_6_out, not_7_out, not_8_out,
       not_9_out, not_10_out, not_11_out, not_12_out, not_13_out, not_14_out, not_15_out, not_16_out,
       not_17_out, not_18_out, not_19_out, not_20_out, not_21_out, not_22_out, or_1_out, or_2_out, or_3_out,
       or_4_out, or_5_out;

  not not_1 (not_1_out, in_1);
  not not_2 (not_2_out, in_2);
  and and_1 (and_1_out, not_1_out, not_2_out);
  not not_3 (not_3_out, D);
  not not_4 (not_4_out, A);
  not not_5 (not_5_out, D);
  not not_6 (not_6_out, A);
  not not_7 (not_7_out, B);
  not not_8 (not_8_out, C);
  not not_9 (not_9_out, A);
  not not_10 (not_10_out, B);
  not not_11 (not_11_out, D);
  not not_12 (not_12_out, A);
  not not_13 (not_13_out, B);
  not not_14 (not_14_out, A);
  not not_15 (not_15_out, C);
  not not_16 (not_16_out, B);
  not not_17 (not_17_out, D);
  not not_18 (not_18_out, B);
  and B_nC (B_nC_out, C, not_3_out, not_4_out);
  and A_nC (A_nC_out, B, not_5_out, not_6_out);
  and nA_nB_C (nA_nB_C_out, not_7_out, not_8_out, D, not_9_out);
  and nA_B_nC (nA_B_nC_out, not_10_out, C, not_11_out, not_12_out);
  and nA_B__C (nA_B__C_out, not_13_out, C, D, not_14_out);
  not not_19 (not_19_out, A);
  not not_20 (not_20_out, D);
  not not_21 (not_21_out, C);
  not not_22 (not_22_out, B);
  and and_2 (and_2_out, D, not_15_out, not_16_out, A);
  and and_3 (and_3_out, not_17_out, C, not_18_out, A);
  or or_1 (or_1_out, B_nC_out, A_nC_out, nA_nB_C_out);
  or or_2 (or_2_out, B_nC_out, A_nC_out);
  or or_3 (or_3_out, B, and_2_out, C);
  or or_4 (or_4_out, nA_B_nC_out, and_2_out);
  or or_5 (or_5_out, nA_B__C_out, and_2_out);
  and A_B (A_B_out, B, C, not_19_out);
  and and_4 (and_4_out, not_20_out, not_21_out, not_22_out, A);
  and and_5 (WR_ACC, and_1_out, or_3_out);
  and and_6 (SEL_OP_1, and_1_out, or_4_out);
  and and_7 (SEL_OP_0, and_1_out, or_5_out);
  and and_8 (SEL_OP2, and_1_out, A_nC_out);
  and and_9 (SEL_ULA, and_1_out, A_B_out);
  and and_10 (SEL_J, and_1_out, and_4_out);
  and and_11 (SEL_TEC, and_1_out, and_2_out);
  and and_12 (SEL_MON, and_1_out, and_3_out);
  and and_13 (EN_RAM, and_1_out, or_1_out);
  and and_14 (WR_RAM, and_1_out, nA_nB_C_out);
  and and_15 (RD_RAM, and_1_out, or_2_out);

  assign EN_PC = 1'b1;
endmodule
